# Fritzing sketch SLAVE_HW_DESIGN (saved by Fritzing 0.9.3b)
breadboards: 2

parts:
  MC1 = Arduino Pro Mini (5V)
  IC1 = MAX485 [package=dil08]
  J1 = screw terminal, 3 pins
  J2 = screw terminal, 3 pins
  R9 = Resistor [tolerance=±5% resistance=10k package=THT]
  R10 = Resistor [tolerance=±5% resistance=10k package=THT]
  R11 = Resistor [tolerance=±5% resistance=10k package=THT]
  R12 = Resistor [tolerance=±5% resistance=10k package=THT]
  R13 = Resistor [tolerance=±5% resistance=100 package=THT]
  R14 = Resistor [tolerance=±5% resistance=22k package=THT]
  R15 = Resistor [tolerance=±5% resistance=22k package=THT]

nets:
  GND: MC1.GND, IC1.GND, J1.pin3, J2.pin3, R15.Pin_1
  VCC: MC1.VCC, IC1.VCC, R9.Pin_1, R10.Pin_1, R11.Pin_1, R12.Pin_1, R14.Pin_0
  N1: MC1.D3, IC1.DE, R11.Pin_0
  N2: MC1.D2, IC1.RE, R10.Pin_0
  N3: MC1.RXI, IC1.DI, R12.Pin_0
  N4: MC1.TXO, IC1.RO, R9.Pin_0
  N5: IC1.A, J1.pin1, J2.pin1, R13.Pin_1, R14.Pin_1
  N6: IC1.B, J1.pin2, J2.pin2, R13.Pin_0, R15.Pin_0

notes:
  Design is Incomplete.
  Please See Read Me file in the GitHub Repository for proper attribution
